// Digital circuit register-file.dig as structural Verilog
module register_file (
  input  [4:0] ReadReg1,
  input  [4:0] ReadReg2,
  input  [4:0] WriteReg,
  input  [31:0] WriteData,
  input  RegWrite,
  input  Clock,
  output [31:0] ReadData1,
  output [31:0] ReadData2
);

  wire Enable_1, Enable_2, Enable_3, Enable_4, Enable_5, Enable_6, Enable_7, Enable_8, Enable_9, Enable_10,
       Enable_11, Enable_12, Enable_13, Enable_14, Enable_15, Enable_16, Enable_17, Enable_18, Enable_19,
       Enable_20, Enable_21, Enable_22, Enable_23, Enable_24, Enable_25, Enable_26, Enable_27, Enable_28,
       Enable_29, Enable_30, Enable_31;
  wire [4:0] multiplexer_1_out;
  wire [31:0] Read_0, Read_1, Read_2, Read_3, Read_4, Read_5, Read_6, Read_7, Read_8, Read_9, Read_10,
       Read_11, Read_12, Read_13, Read_14, Read_15, Read_16, Read_17, Read_18, Read_19, Read_20, Read_21,
       Read_22, Read_23, Read_24, Read_25, Read_26, Read_27, Read_28, Read_29, Read_30, Read_31;

  Decoder #(.Selector_Bits(5)) decoder_1 (
    .sel(multiplexer_1_out), .out_1(Enable_1), .out_2(Enable_2), .out_3(Enable_3), .out_4(Enable_4),
    .out_5(Enable_5), .out_6(Enable_6), .out_7(Enable_7), .out_8(Enable_8), .out_9(Enable_9),
    .out_10(Enable_10), .out_11(Enable_11), .out_12(Enable_12), .out_13(Enable_13), .out_14(Enable_14),
    .out_15(Enable_15), .out_16(Enable_16), .out_17(Enable_17), .out_18(Enable_18), .out_19(Enable_19),
    .out_20(Enable_20), .out_21(Enable_21), .out_22(Enable_22), .out_23(Enable_23), .out_24(Enable_24),
    .out_25(Enable_25), .out_26(Enable_26), .out_27(Enable_27), .out_28(Enable_28), .out_29(Enable_29),
    .out_30(Enable_30), .out_31(Enable_31));  // open: out_0
  Multiplexer #(.Bits(5)) multiplexer_1 (.sel(RegWrite), .in_0({5{1'b0}}), .in_1(WriteReg), .out(multiplexer_1_out));
  Register #(.Bits(32)) Reg_0 (.D({32{1'b0}}), .C(Clock), .en(1'b1), .Q(Read_0));
  Register #(.Bits(32)) Reg_4 (.D(WriteData), .C(Clock), .en(Enable_4), .Q(Read_4));
  Register #(.Bits(32)) Reg_8 (.D(WriteData), .C(Clock), .en(Enable_8), .Q(Read_8));
  Register #(.Bits(32)) Reg_12 (.D(WriteData), .C(Clock), .en(Enable_12), .Q(Read_12));
  Register #(.Bits(32)) Reg_16 (.D(WriteData), .C(Clock), .en(Enable_16), .Q(Read_16));
  Register #(.Bits(32)) Reg_20 (.D(WriteData), .C(Clock), .en(Enable_20), .Q(Read_20));
  Register #(.Bits(32)) Reg_24 (.D(WriteData), .C(Clock), .en(Enable_24), .Q(Read_24));
  Register #(.Bits(32)) Reg_28 (.D(WriteData), .C(Clock), .en(Enable_28), .Q(Read_28));
  Register #(.Bits(32)) Reg_1 (.D(WriteData), .C(Clock), .en(Enable_1), .Q(Read_1));
  Register #(.Bits(32)) Reg_5 (.D(WriteData), .C(Clock), .en(Enable_5), .Q(Read_5));
  Register #(.Bits(32)) Reg_9 (.D(WriteData), .C(Clock), .en(Enable_9), .Q(Read_9));
  Register #(.Bits(32)) Reg_13 (.D(WriteData), .C(Clock), .en(Enable_13), .Q(Read_13));
  Register #(.Bits(32)) Reg_17 (.D(WriteData), .C(Clock), .en(Enable_17), .Q(Read_17));
  Register #(.Bits(32)) Reg_21 (.D(WriteData), .C(Clock), .en(Enable_21), .Q(Read_21));
  Register #(.Bits(32)) Reg_25 (.D(WriteData), .C(Clock), .en(Enable_25), .Q(Read_25));
  Register #(.Bits(32)) Reg_29 (.D(WriteData), .C(Clock), .en(Enable_29), .Q(Read_29));
  Register #(.Bits(32)) Reg_2 (.D(WriteData), .C(Clock), .en(Enable_2), .Q(Read_2));
  Register #(.Bits(32)) Reg_6 (.D(WriteData), .C(Clock), .en(Enable_6), .Q(Read_6));
  Register #(.Bits(32)) Reg_10 (.D(WriteData), .C(Clock), .en(Enable_10), .Q(Read_10));
  Register #(.Bits(32)) Reg_14 (.D(WriteData), .C(Clock), .en(Enable_14), .Q(Read_14));
  Register #(.Bits(32)) Reg_18 (.D(WriteData), .C(Clock), .en(Enable_18), .Q(Read_18));
  Register #(.Bits(32)) Reg_22 (.D(WriteData), .C(Clock), .en(Enable_22), .Q(Read_22));
  Register #(.Bits(32)) Reg_26 (.D(WriteData), .C(Clock), .en(Enable_26), .Q(Read_26));
  Register #(.Bits(32)) Reg_30 (.D(WriteData), .C(Clock), .en(Enable_30), .Q(Read_30));
  Register #(.Bits(32)) Reg_3 (.D(WriteData), .C(Clock), .en(Enable_3), .Q(Read_3));
  Register #(.Bits(32)) Reg_7 (.D(WriteData), .C(Clock), .en(Enable_7), .Q(Read_7));
  Register #(.Bits(32)) Reg_11 (.D(WriteData), .C(Clock), .en(Enable_11), .Q(Read_11));
  Register #(.Bits(32)) Reg_15 (.D(WriteData), .C(Clock), .en(Enable_15), .Q(Read_15));
  Register #(.Bits(32)) Reg_19 (.D(WriteData), .C(Clock), .en(Enable_19), .Q(Read_19));
  Register #(.Bits(32)) Reg_23 (.D(WriteData), .C(Clock), .en(Enable_23), .Q(Read_23));
  Register #(.Bits(32)) Reg_27 (.D(WriteData), .C(Clock), .en(Enable_27), .Q(Read_27));
  Register #(.Bits(32)) Reg_31 (.D(WriteData), .C(Clock), .en(Enable_31), .Q(Read_31));
  Multiplexer #(.Selector_Bits(5), .Bits(32)) multiplexer_2 (
    .sel(ReadReg1), .in_0(Read_0), .in_1(Read_1), .in_2(Read_2), .in_3(Read_3), .in_4(Read_4), .in_5(Read_5),
    .in_6(Read_6), .in_7(Read_7), .in_8(Read_8), .in_9(Read_9), .in_10(Read_10), .in_11(Read_11),
    .in_12(Read_12), .in_13(Read_13), .in_14(Read_14), .in_15(Read_15), .in_16(Read_16), .in_17(Read_17),
    .in_18(Read_18), .in_19(Read_19), .in_20(Read_20), .in_21(Read_21), .in_22(Read_22), .in_23(Read_23),
    .in_24(Read_24), .in_25(Read_25), .in_26(Read_26), .in_27(Read_27), .in_28(Read_28), .in_29(Read_29),
    .in_30(Read_30), .in_31(Read_31), .out(ReadData1));
  Multiplexer #(.Selector_Bits(5), .Bits(32)) multiplexer_3 (
    .sel(ReadReg2), .in_0(Read_0), .in_1(Read_1), .in_2(Read_2), .in_3(Read_3), .in_4(Read_4), .in_5(Read_5),
    .in_6(Read_6), .in_7(Read_7), .in_8(Read_8), .in_9(Read_9), .in_10(Read_10), .in_11(Read_11),
    .in_12(Read_12), .in_13(Read_13), .in_14(Read_14), .in_15(Read_15), .in_16(Read_16), .in_17(Read_17),
    .in_18(Read_18), .in_19(Read_19), .in_20(Read_20), .in_21(Read_21), .in_22(Read_22), .in_23(Read_23),
    .in_24(Read_24), .in_25(Read_25), .in_26(Read_26), .in_27(Read_27), .in_28(Read_28), .in_29(Read_29),
    .in_30(Read_30), .in_31(Read_31), .out(ReadData2));
endmodule

/* Test case Register File Test:
WriteReg WriteData RegWrite Clock ReadReg1 ReadReg2 ReadData1 ReadData2

# $1 = 25
1 25 1 C 1 0 25 0

# $2 = 30
2 30 1 C 0 2 0 30

# $(N+1) = (N+1)
loop(N, 30)
	(N+1) (N+1) 1 C (N+1) (N) (N+1) (N)
end loop

# $(N+1) = N-60
loop(N, 30)
	(N+1) (N-60) 1 C (N+1) (N+1) (N-60) (N-60)
end loop

# Try writing to $0. This should not write anything
0 25 1 C 0 0 0 0

# try writing when RegWrite = 0
# (the registers should still have their old values)
loop(N, 30)
	(N+1) (N+80) 0 C (N+1) (N+1) (N-60) (N-60)
end loop
*/
